# Fritzing sketch traffigo (saved by Fritzing 0.9.3b)

parts:
  hc-sr1 = hc-sr04
  J1 = Piezo Speaker
  J2 = Screw terminal - 2 pins [package=THT]
  Nano = Arduino Nano (Rev3.0) (ICSP)

nets:
  VCC: hc-sr1.VCC, Nano.5V
  N1: hc-sr1.Trig, Nano.D9
  N2: hc-sr1.Echo, Nano.D10
  GND: hc-sr1.GND, J1.pin1, J2.pin2, Nano.GND
  N3: J1.pin2, Nano.D8
  N4: J2.pin1, Nano.VIN

notes:
  +12VDC GND
  TRAFIIGO
